# Fritzing sketch SPI_Master_Slave_LEDx8_ATMega88V (saved by Fritzing 0.9.3b)
breadboards: 2

parts:
  LED1 = LED - 3mm [color="Red (633nm)" package="3 mm [THT]"]
  LED2 = LED - 3mm [color="Red (633nm)" package="3 mm [THT]"]
  LED3 = LED - 3mm [color="Red (633nm)" package="3 mm [THT]"]
  LED4 = LED - 3mm [color="Red (633nm)" package="3 mm [THT]"]
  LED5 = LED - 3mm [color="Red (633nm)" package="3 mm [THT]"]
  LED6 = LED - 3mm [color="Red (633nm)" package="3 mm [THT]"]
  LED7 = LED - 3mm [color="Red (633nm)" package="3 mm [THT]"]
  LED8 = LED - 3mm [color="Red (633nm)" package="3 mm [THT]"]
  R1 = Resistor [tolerance=±5% resistance=1k package=THT]
  R2 = Resistor [tolerance=±5% resistance=1k package=THT]
  R3 = Resistor [tolerance=±5% resistance=1k package=THT]
  R4 = Resistor [tolerance=±5% resistance=1k package=THT]
  R5 = Resistor [tolerance=±5% resistance=1k package=THT]
  R6 = Resistor [tolerance=±5% resistance=1k package=THT]
  R7 = Resistor [tolerance=±5% resistance=1k package=THT]
  R8 = Resistor [tolerance=±5% resistance=1k package=THT]
  パーツ2 = Arduino Uno (Rev3)
  U1 = atmega168 [package=dip]
  C1 = Electrolytic Capacitor [capacitance=1µF package="100 mil [THT, electrolytic]"]
  C2 = Ceramic Capacitor [capacitance=100nF package="100 mil [THT, multilayer]"]
  C3 = Ceramic Capacitor [capacitance=100nF package="100 mil [THT, multilayer]"]

nets:
  N1: LED1.cathode, R1.Pin_0
  N2: LED1.anode, U1.D0_(RX)
  N3: LED2.cathode, R2.Pin_0
  N4: LED2.anode, U1.D1_(TX)
  N5: LED3.cathode, R3.Pin_0
  N6: LED3.anode, U1.D2
  N7: LED4.cathode, R4.Pin_0
  N8: LED4.anode, U1.D3_(PWM)
  N9: LED5.cathode, R5.Pin_0
  N10: LED5.anode, U1.D4
  N11: LED6.cathode, R6.Pin_0
  N12: LED6.anode, U1.D5_(PWM)
  N13: LED7.cathode, R7.Pin_0
  N14: LED7.anode, U1.D6_(PWM)
  N15: LED8.cathode, R8.Pin_0
  N16: LED8.anode, U1.D7
  GND: R1.Pin_1, R2.Pin_1, R3.Pin_1, R4.Pin_1, R5.Pin_1, R6.Pin_1, R7.Pin_1, R8.Pin_1, パーツ2.GND, U1.GND, C1.-, C2.0, C3.1
  N17: パーツ2.D10_PWM/SS, U1.D10_(PWM)
  N18: パーツ2.D11_PWM/MOSI, U1.D11_(PWM)
  N19: パーツ2.D12/MISO, U1.D12
  N20: パーツ2.D13/SCK, U1.D13
  5V: パーツ2.5V, U1.VCC, U1.AVCC, C1.+, C2.1, C3.0
