# Fritzing sketch SPI_Master_Slave_LEDx8_Arduino (saved by Fritzing 0.9.3b)
breadboards: 1

parts:
  パーツ1 = Arduino Uno (Rev3)
  LED1 = LED - 3mm [color="Red (633nm)" package="3 mm [THT]"]
  LED2 = LED - 3mm [color="Red (633nm)" package="3 mm [THT]"]
  LED3 = LED - 3mm [color="Red (633nm)" package="3 mm [THT]"]
  LED4 = LED - 3mm [color="Red (633nm)" package="3 mm [THT]"]
  LED5 = LED - 3mm [color="Red (633nm)" package="3 mm [THT]"]
  LED6 = LED - 3mm [color="Red (633nm)" package="3 mm [THT]"]
  LED7 = LED - 3mm [color="Red (633nm)" package="3 mm [THT]"]
  LED8 = LED - 3mm [color="Red (633nm)" package="3 mm [THT]"]
  R1 = Resistor [tolerance=±5% resistance=1k package=THT]
  R2 = Resistor [tolerance=±5% resistance=1k package=THT]
  R3 = Resistor [tolerance=±5% resistance=1k package=THT]
  R4 = Resistor [tolerance=±5% resistance=1k package=THT]
  R5 = Resistor [tolerance=±5% resistance=1k package=THT]
  R6 = Resistor [tolerance=±5% resistance=1k package=THT]
  R7 = Resistor [tolerance=±5% resistance=1k package=THT]
  R8 = Resistor [tolerance=±5% resistance=1k package=THT]
  パーツ2 = Arduino Uno (Rev3)

nets:
  N1: パーツ1.D10_PWM/SS, パーツ2.D10_PWM/SS
  N2: パーツ1.D11_PWM/MOSI, パーツ2.D11_PWM/MOSI
  N3: パーツ1.D12/MISO, パーツ2.D12/MISO
  N4: パーツ1.D13/SCK, パーツ2.D13/SCK
  GND: パーツ1.GND, R1.Pin_1, R2.Pin_1, R3.Pin_1, R4.Pin_1, R5.Pin_1, R6.Pin_1, R7.Pin_1, R8.Pin_1, パーツ2.GND
  N5: パーツ1.D0/RX, LED1.anode
  N6: パーツ1.D1/TX, LED2.anode
  N7: パーツ1.D2, LED3.anode
  N8: パーツ1.D3_PWM, LED4.anode
  N9: パーツ1.D4, LED5.anode
  N10: パーツ1.D5_PWM, LED6.anode
  N11: パーツ1.D6_PWM, LED7.anode
  N12: パーツ1.D7, LED8.anode
  N13: LED1.cathode, R1.Pin_0
  N14: LED2.cathode, R2.Pin_0
  N15: LED3.cathode, R3.Pin_0
  N16: LED4.cathode, R4.Pin_0
  N17: LED5.cathode, R5.Pin_0
  N18: LED6.cathode, R6.Pin_0
  N19: LED7.cathode, R7.Pin_0
  N20: LED8.cathode, R8.Pin_0

notes:
  Slave
  Master
